// Digital circuit part_c.dig as structural Verilog
module part_c (
  input  in_0,
  input  in_1,
  input  in_2,
  output out_0
);

  wire fgnfet_3_s, fgpfet_1_s, fgpfet_3_s, nfet_4_s, nfet_6_s, nfet_9_s, nfet_11_s, nfet_13_s, nfet_16_s,
       nfet_22_s, nfet_25_s, nfet_27_s, nfet_30_s, pfet_1_d, pfet_2_d, pfet_3_d, pfet_4_d, pfet_5_d,
       pfet_6_d, pfet_7_d, pfet_8_d, pfet_11_d, pfet_12_d, pfet_13_d, pfet_16_d, pfet_17_d, pfet_18_d,
       pfet_19_d, pfet_20_d, pfet_21_d, pfet_22_d, pfet_25_d, pfet_26_d, pfet_27_d, pfet_30_d, pfet_31_d;

  PFET pfet_1 (.G(in_2), .S(1'b1), .D(pfet_1_d));
  FGNFET fgnfet_1 (.G(in_2), .D(pfet_1_d), .S(1'b0));
  PFET pfet_2 (.G(pfet_1_d), .S(1'b1), .D(pfet_2_d));
  NFET nfet_1 (.G(pfet_1_d), .D(pfet_2_d), .S(1'b0));
  PFET pfet_3 (.G(in_2), .S(1'b1), .D(pfet_3_d));
  FGNFET fgnfet_2 (.G(in_2), .D(pfet_3_d), .S(1'b0));
  PFET pfet_4 (.G(in_0), .S(1'b1), .D(pfet_4_d));
  NFET nfet_2 (.G(in_0), .D(pfet_4_d), .S(1'b0));
  FGPFET fgpfet_1 (.G(in_0), .S(fgpfet_1_s), .D(1'b0));
  PFET pfet_5 (.G(pfet_3_d), .S(1'b1), .D(pfet_5_d));
  NFET nfet_3 (.G(pfet_3_d), .D(pfet_5_d), .S(1'b0));
  NFET nfet_4 (.G(in_0), .D(1'b1), .S(nfet_4_s));
  NFET nfet_5 (.G(pfet_1_d), .D(nfet_4_s), .S(fgpfet_1_s));
  FGPFET fgpfet_2 (.G(pfet_1_d), .S(fgpfet_1_s), .D(1'b0));
  PFET pfet_6 (.G(pfet_1_d), .S(1'b1), .D(pfet_6_d));
  PFET pfet_7 (.G(pfet_2_d), .S(pfet_6_d), .D(pfet_7_d));
  NFET nfet_6 (.G(pfet_2_d), .D(pfet_7_d), .S(nfet_6_s));
  NFET nfet_7 (.G(in_0), .D(nfet_6_s), .S(1'b0));
  PFET pfet_8 (.G(in_1), .S(1'b1), .D(pfet_8_d));
  NFET nfet_8 (.G(in_1), .D(pfet_8_d), .S(1'b0));
  FGPFET fgpfet_3 (.G(in_1), .S(fgpfet_3_s), .D(1'b0));
  NFET nfet_9 (.G(pfet_1_d), .D(pfet_7_d), .S(nfet_9_s));
  NFET nfet_10 (.G(pfet_4_d), .D(nfet_9_s), .S(1'b0));
  NFET nfet_11 (.G(in_1), .D(1'b1), .S(nfet_11_s));
  NFET nfet_12 (.G(pfet_3_d), .D(nfet_11_s), .S(fgpfet_3_s));
  FGPFET fgpfet_4 (.G(pfet_3_d), .S(fgpfet_3_s), .D(1'b0));
  PFET pfet_9 (.G(pfet_4_d), .S(1'b1), .D(pfet_6_d));
  PFET pfet_10 (.G(in_0), .S(pfet_6_d), .D(pfet_7_d));
  PFET pfet_11 (.G(pfet_3_d), .S(1'b1), .D(pfet_11_d));
  PFET pfet_12 (.G(pfet_5_d), .S(pfet_11_d), .D(pfet_12_d));
  NFET nfet_13 (.G(pfet_5_d), .D(pfet_12_d), .S(nfet_13_s));
  NFET nfet_14 (.G(in_1), .D(nfet_13_s), .S(1'b0));
  PFET pfet_13 (.G(pfet_7_d), .S(1'b1), .D(pfet_13_d));
  NFET nfet_15 (.G(pfet_7_d), .D(pfet_13_d), .S(1'b0));
  NFET nfet_16 (.G(pfet_3_d), .D(pfet_12_d), .S(nfet_16_s));
  NFET nfet_17 (.G(pfet_8_d), .D(nfet_16_s), .S(1'b0));
  PFET pfet_14 (.G(pfet_8_d), .S(1'b1), .D(pfet_11_d));
  PFET pfet_15 (.G(in_1), .S(pfet_11_d), .D(pfet_12_d));
  PFET pfet_16 (.G(pfet_12_d), .S(1'b1), .D(pfet_16_d));
  NFET nfet_18 (.G(pfet_12_d), .D(pfet_16_d), .S(1'b0));
  PFET pfet_17 (.G(fgpfet_1_s), .S(1'b1), .D(pfet_17_d));
  NFET nfet_19 (.G(fgpfet_1_s), .D(pfet_17_d), .S(1'b0));
  PFET pfet_18 (.G(pfet_13_d), .S(1'b1), .D(pfet_18_d));
  NFET nfet_20 (.G(pfet_13_d), .D(pfet_18_d), .S(1'b0));
  PFET pfet_19 (.G(fgpfet_3_s), .S(1'b1), .D(pfet_19_d));
  NFET nfet_21 (.G(fgpfet_3_s), .D(pfet_19_d), .S(1'b0));
  PFET pfet_20 (.G(fgpfet_1_s), .S(1'b1), .D(pfet_20_d));
  PFET pfet_21 (.G(pfet_17_d), .S(pfet_20_d), .D(pfet_21_d));
  NFET nfet_22 (.G(pfet_17_d), .D(pfet_21_d), .S(nfet_22_s));
  NFET nfet_23 (.G(pfet_13_d), .D(nfet_22_s), .S(1'b0));
  PFET pfet_22 (.G(pfet_16_d), .S(1'b1), .D(pfet_22_d));
  NFET nfet_24 (.G(pfet_16_d), .D(pfet_22_d), .S(1'b0));
  NFET nfet_25 (.G(fgpfet_1_s), .D(pfet_21_d), .S(nfet_25_s));
  NFET nfet_26 (.G(pfet_18_d), .D(nfet_25_s), .S(1'b0));
  PFET pfet_23 (.G(pfet_18_d), .S(1'b1), .D(pfet_20_d));
  PFET pfet_24 (.G(pfet_13_d), .S(pfet_20_d), .D(pfet_21_d));
  PFET pfet_25 (.G(fgpfet_3_s), .S(1'b1), .D(pfet_25_d));
  PFET pfet_26 (.G(pfet_19_d), .S(pfet_25_d), .D(pfet_26_d));
  NFET nfet_27 (.G(pfet_19_d), .D(pfet_26_d), .S(nfet_27_s));
  NFET nfet_28 (.G(pfet_16_d), .D(nfet_27_s), .S(1'b0));
  PFET pfet_27 (.G(pfet_21_d), .S(1'b1), .D(pfet_27_d));
  NFET nfet_29 (.G(pfet_21_d), .D(pfet_27_d), .S(1'b0));
  NFET nfet_30 (.G(fgpfet_3_s), .D(pfet_26_d), .S(nfet_30_s));
  NFET nfet_31 (.G(pfet_22_d), .D(nfet_30_s), .S(1'b0));
  PFET pfet_28 (.G(pfet_22_d), .S(1'b1), .D(pfet_25_d));
  PFET pfet_29 (.G(pfet_16_d), .S(pfet_25_d), .D(pfet_26_d));
  PFET pfet_30 (.G(pfet_26_d), .S(1'b1), .D(pfet_30_d));
  NFET nfet_32 (.G(pfet_26_d), .D(pfet_30_d), .S(1'b0));
  PFET pfet_31 (.G(pfet_30_d), .S(1'b1), .D(pfet_31_d));
  PFET pfet_32 (.G(pfet_27_d), .S(1'b1), .D(pfet_31_d));
  FGNFET fgnfet_3 (.G(pfet_30_d), .D(pfet_31_d), .S(fgnfet_3_s));
  FGNFET fgnfet_4 (.G(pfet_27_d), .D(fgnfet_3_s), .S(1'b0));
  PFET pfet_33 (.G(pfet_31_d), .S(1'b1), .D(out_0));
  FGNFET fgnfet_5 (.G(pfet_31_d), .D(out_0), .S(1'b0));

  // Notes on the sheet:
  //   X
  //   Y
endmodule

/* Test case part_c_test:
in_0 in_1 in_2 out_0
 0    0    0    1
 0    0    1    0
 0    1    0    1
 0    1    1    0
 1    0    0    1
 1    0    1    0
 1    1    0    1
 1    1    1    1
*/
