// Digital circuit lab2_part2.dig as structural Verilog
module lab2_part2 (
  input  in0,
  input  in1,
  input  in2,
  input  in3,
  output seg_a,
  output seg_f,
  output seg_b,
  output seg_g,
  output seg_e,
  output seg_c,
  output seg_d,
  output seg_dp,
  output sign_a,
  output sign_f,
  output sign_b,
  output sign_g,
  output sign_e,
  output sign_c,
  output sign_d,
  output sign_dp
);

  wire m0, m1, m2, m3, multiplexer_1_out, multiplexer_4_out, multiplexer_7_out, multiplexer_10_out,
       not_1_out, not_2_out, not_3_out, not_4_out, not_5_out, not_6_out, not_7_out, not_8_out, not_9_out,
       not_10_out, not_11_out, not_12_out, not_13_out, not_14_out, not_15_out, not_16_out, not_17_out,
       not_18_out, not_19_out, not_20_out, not_21_out, not_22_out, not_23_out, not_24_out, not_25_out,
       not_26_out, not_27_out, not_28_out, not_29_out, not_30_out, not_31_out, not_32_out, not_33_out,
       not_34_out, not_35_out, not_36_out, not_37_out, not_38_out, not_39_out, not_40_out, not_41_out,
       not_42_out, not_43_out, not_44_out, or_1_out, or_2_out, or_3_out, or_5_out, or_6_out, or_7_out,
       or_8_out, or_9_out, or_10_out, or_11_out, or_12_out, or_13_out, or_14_out, or_15_out, or_16_out,
       or_17_out, or_18_out, or_19_out, or_20_out;
  wire [1:1] multiplexer_2_out, multiplexer_5_out, multiplexer_8_out;

  not not_1 (not_1_out, m2);
  not not_2 (not_2_out, m2);
  not not_3 (not_3_out, m1);
  not not_4 (not_4_out, m1);
  not not_5 (not_5_out, m2);
  not not_6 (not_6_out, m1);
  not not_7 (not_7_out, m0);
  not not_8 (not_8_out, m2);
  not not_9 (not_9_out, m0);
  not not_10 (not_10_out, m0);
  or or_1 (or_1_out, m3, not_11_out, m1, m0);
  not not_11 (not_11_out, m2);
  or or_2 (or_2_out, m3, not_1_out, m1, not_12_out);
  not not_12 (not_12_out, m0);
  or or_3 (or_3_out, m3, not_2_out, not_3_out, m0);
  or or_4 (seg_c, m3, m2, not_4_out, m0);
  or or_5 (or_5_out, m3, m2, m1, not_10_out);
  or or_6 (or_6_out, m3, not_5_out, not_6_out, not_7_out);
  or or_7 (or_7_out, m3, not_8_out, m1, m0);
  or or_8 (or_8_out, m3, m2, m1, not_9_out);
  and and_1 (seg_a, or_5_out, or_1_out);
  and and_2 (seg_b, or_2_out, or_3_out);
  and and_3 (seg_d, or_6_out, or_7_out, or_8_out);
  not not_13 (not_13_out, in0);
  Multiplexer #(.Selector_Bits(2)) multiplexer_1 (
    .sel(2'b01), .in_0(not_13_out), .in_1(not_14_out), .in_2(not_15_out), .in_3(not_13_out),
    .out(multiplexer_1_out));
  not not_14 (not_14_out, not_13_out);
  not not_15 (not_15_out, not_13_out);
  Multiplexer #(.Selector_Bits(2)) multiplexer_2 (
    .sel(2'b01), .in_0(1'b0), .in_1(not_13_out), .in_2(not_13_out), .in_3(1'b1), .out(multiplexer_2_out[1]));
  Multiplexer multiplexer_3 (.sel(in3), .in_0(in0), .in_1(multiplexer_1_out), .out(m0));
  not not_16 (not_16_out, m2);
  not not_17 (not_17_out, m1);
  not not_18 (not_18_out, m0);
  not not_19 (not_19_out, m1);
  not not_20 (not_20_out, m0);
  not not_21 (not_21_out, m2);
  not not_22 (not_22_out, m0);
  not not_23 (not_23_out, m2);
  not not_24 (not_24_out, m0);
  not not_25 (not_25_out, in1);
  not not_26 (not_26_out, not_25_out);
  not not_27 (not_27_out, not_25_out);
  or or_9 (or_9_out, m3, not_16_out, not_17_out, not_18_out);
  or or_10 (or_10_out, m3, not_21_out, m1, not_22_out);
  or or_11 (or_11_out, m3, not_23_out, m1, m0);
  or or_12 (or_12_out, m3, m2, not_19_out, not_20_out);
  or or_13 (or_13_out, m3, m2, m1, not_24_out);
  Multiplexer #(.Selector_Bits(2)) multiplexer_4 (
    .sel({multiplexer_2_out[1], 1'b0}), .in_0(not_25_out), .in_1(not_26_out), .in_2(not_27_out),
    .in_3(not_25_out), .out(multiplexer_4_out));
  Multiplexer #(.Selector_Bits(2)) multiplexer_5 (
    .sel({multiplexer_2_out[1], 1'b0}), .in_0(1'b0), .in_1(not_25_out), .in_2(not_25_out), .in_3(1'b1),
    .out(multiplexer_5_out[1]));
  and and_4 (seg_e, or_9_out, or_10_out, or_11_out, or_12_out, or_13_out);
  Multiplexer multiplexer_6 (.sel(in3), .in_0(in1), .in_1(multiplexer_4_out), .out(m1));
  not not_28 (not_28_out, in2);
  Multiplexer #(.Selector_Bits(2)) multiplexer_7 (
    .sel({multiplexer_5_out[1], 1'b0}), .in_0(not_28_out), .in_1(not_29_out), .in_2(not_30_out),
    .in_3(not_28_out), .out(multiplexer_7_out));
  not not_29 (not_29_out, not_28_out);
  not not_30 (not_30_out, not_28_out);
  not not_31 (not_31_out, m2);
  not not_32 (not_32_out, m1);
  not not_33 (not_33_out, m0);
  not not_34 (not_34_out, m1);
  not not_35 (not_35_out, m0);
  not not_36 (not_36_out, m1);
  not not_37 (not_37_out, m0);
  Multiplexer #(.Selector_Bits(2)) multiplexer_8 (
    .sel({multiplexer_5_out[1], 1'b0}), .in_0(1'b0), .in_1(not_28_out), .in_2(not_28_out), .in_3(1'b1),
    .out(multiplexer_8_out[1]));
  or or_14 (or_14_out, m3, not_31_out, not_32_out, not_33_out);
  or or_15 (or_15_out, m3, m2, not_34_out, not_35_out);
  or or_16 (or_16_out, m3, m2, not_36_out, m0);
  or or_17 (or_17_out, m3, m2, m1, not_37_out);
  Multiplexer multiplexer_9 (.sel(in3), .in_0(in2), .in_1(multiplexer_7_out), .out(m2));
  and and_5 (seg_f, or_14_out, or_15_out, or_16_out, or_17_out);
  not not_38 (not_38_out, in3);
  not not_39 (not_39_out, not_38_out);
  not not_40 (not_40_out, not_38_out);
  Multiplexer #(.Selector_Bits(2)) multiplexer_10 (
    .sel({multiplexer_8_out[1], 1'b0}), .in_0(not_38_out), .in_1(not_39_out), .in_2(not_40_out),
    .in_3(not_38_out), .out(multiplexer_10_out));
  not not_41 (not_41_out, m2);
  not not_42 (not_42_out, m1);
  not not_43 (not_43_out, m0);
  Multiplexer #(.Selector_Bits(2)) multiplexer_11 (
    .sel({multiplexer_8_out[1], 1'b0}), .in_0(1'b0), .in_1(not_38_out), .in_2(not_38_out), .in_3(1'b1));  // open: out
  not not_44 (not_44_out, m0);
  Multiplexer multiplexer_12 (.sel(in3), .in_0(in3), .in_1(multiplexer_10_out), .out(m3));
  or or_18 (or_18_out, m3, m2, m1, m0);
  or or_19 (or_19_out, m3, m2, m1, not_44_out);
  or or_20 (or_20_out, m3, not_41_out, not_42_out, not_43_out);
  and and_6 (seg_g, or_18_out, or_19_out, or_20_out);
  Seven_Seg seven_seg_1 (.a(1'b0), .b(1'b0), .c(1'b0), .d(1'b0), .e(1'b0), .f(1'b0), .g(in3), .dp(1'b0));
  Seven_Seg seven_seg_2 (.a(seg_a), .b(seg_b), .c(seg_c), .d(seg_d), .e(seg_e), .f(seg_f), .g(seg_g), .dp(1'b0));

  assign seg_dp = 1'b0;
  assign sign_a = 1'b0;
  assign sign_b = 1'b0;
  assign sign_c = 1'b0;
  assign sign_d = 1'b0;
  assign sign_dp = 1'b0;
  assign sign_e = 1'b0;
  assign sign_f = 1'b0;
  assign sign_g = in3;

  // Notes on the sheet:
  //   Interface (do not edit the content inside this box)
  //   Outputs:
  //   Inputs
  //   Sign
  //   Decimal Number
endmodule

/* Test case:
in3 in2 in1 in0  sign_a sign_b sign_c sign_d sign_e sign_f sign_g  seg_a seg_b seg_c seg_d seg_e seg_f seg_g
 0   0   0   0    0      0      0      0      0      0      0       1     1     1     1     1     1     0
*/
